# Fritzing sketch Beavers_other (saved by Fritzing 0.9.4)
breadboards: 1

parts:
  LED1 = LED - 5mm [color="Yellow (592nm)" package="5 mm [THT]"]
  R1 = Resistor [tolerance=±5% resistance=220 package=THT]
  LED2 = LED - 5mm [color="Green (555nm)" package="5 mm [THT]"]
  LED3 = LED - 5mm [color="Red (635nm)" package="5 mm [THT]"]
  R3 = Resistor [tolerance=±5% resistance=220 package=THT]
  R4 = Resistor [tolerance=±5% resistance=220 package=THT]
  Digispark1 = Digispark
  LED4 = LED - 5mm [color="Blue (430nm)" package="5 mm [THT]"]
  LED5 = LED - 5mm [color="White (4500K)" package="5 mm [THT]"]
  R5 = Resistor [tolerance=±5% resistance=220 package=THT]
  R6 = Resistor [tolerance=±5% resistance=220 package=THT]
  LED6 = LED - 5mm [color="Green (555nm)" package="5 mm [THT]"]  # not connected

nets:
  N1: LED1.cathode, R3.Pin_0
  GND: LED1.anode, LED2.anode, LED3.anode, Digispark1.GND, Digispark1.VIN, LED4.anode, LED5.anode
  N2: R1.Pin_0, LED2.cathode
  N3: R1.Pin_1, Digispark1.P4
  N4: LED3.cathode, R4.Pin_0
  N5: R3.Pin_1, Digispark1.P3
  N6: R4.Pin_1, Digispark1.P2
  N7: Digispark1.P0, R6.Pin_1
  N8: Digispark1.P1, R5.Pin_1
  N9: LED4.cathode, R5.Pin_0
  N10: LED5.cathode, R6.Pin_0

notes:
  Longer wire of LED (light) always to the left!

custom parts:
  Digispark: The Digispark is an Attiny85 based microcontroller development board similar to the Arduino line, only cheaper, smaller, and a bit less powerful. With a whole host of shields to extend its functionality and the ability to use the familiar Arduino IDE the Digispark is a great way to jump into electronics, or perfect for when an Arduino is too big or too much.
